// Logisim project StickyStacky16.circ as structural Verilog: 7 circuits, main circuit main
// fez
module main (
  input  reset
);

  wire clock, clock_out, ram_load, ram_store, sig_halt;
  wire [1:0] s_spsel, s_wsel, sc_spsel, sc_wsel;
  wire [2:0] alu_1_flags, controller_1_stack_mux;
  wire [3:0] bitselector_1_out;
  wire [5:0] op;
  wire [9:0] valInstr;
  wire [15:0] alu_1_c, bit_extender_1_out, multiplexer_1_out, pc, pc_1, pc_updater_1_next_pc,
       stack_1_stack_sp, stack_2_stack_sp, stack_2_stack_sp_1, tester_1_output, valRam;

  Clock u_clock (.out(clock_out));
  and and_1 (clock, ~sig_halt, clock_out);  // AND_Gate
  assign bit_extender_1_out = {{6{1'b0}}, valInstr};  // Bit_Extender bit_extender_1
  Stack stack_1 (
    .Input(pc_1), .SPsel(sc_spsel), .Wsel(sc_wsel), .stack_sp(stack_1_stack_sp), .Clock(clock), .reset(reset));  // open: stack_sp_1
  Multiplexer #(.select(3), .width(16), .enable("false")) multiplexer_1 (
    .in0(stack_2_stack_sp), .in1(valRam), .in2(bit_extender_1_out), .in3(alu_1_c), .in4(tester_1_output),
    .out(multiplexer_1_out), .sel(controller_1_stack_mux));  // open: in5, in6, in7
  Register #(.width(16)) u_PC (.D(pc_updater_1_next_pc), .Q(pc), .clk(clock), .clr(reset));  // open: en
  Stack stack_2 (
    .Input(multiplexer_1_out), .SPsel(s_spsel), .Wsel(s_wsel), .stack_sp(stack_2_stack_sp),
    .stack_sp_1(stack_2_stack_sp_1), .Clock(clock), .reset(reset));
  PC_updater pc_updater_1 (
    .op(op), .adrInstr(valInstr), .pc(pc), .call_stack(stack_1_stack_sp), .stack_top(stack_2_stack_sp),
    .next_pc(pc_updater_1_next_pc), .pc___1(pc_1));
  BitSelector #(.width(6), .group(4)) bitselector_1 (.in(op), .out(bitselector_1_out), .sel(1'b0));
  ALU alu_1 (
    .A(stack_2_stack_sp), .B(stack_2_stack_sp_1), .op(bitselector_1_out), .C(alu_1_c), .flags(alu_1_flags));  // open: CBout
  Tester tester_1 (.op(op), .flags(alu_1_flags), .\output (tester_1_output));
  Controller controller_1 (
    .op(op), .stackc_wsel(sc_wsel), .stackc_spsel(sc_spsel), .stack_wsel(s_wsel), .stack_spsel(s_spsel),
    .stack_mux(controller_1_stack_mux), .sig_halt(sig_halt), .ram_load(ram_load), .ram_store(ram_store));
  ROM #(.addrWidth(16), .dataWidth(16)) rom_1 (.addr(pc), .data({op, valInstr}));  // open: sel
  RAM #(.addrWidth(16), .dataWidth(16), .bus("separate")) ram_1 (
    .addr(bit_extender_1_out), .din(stack_2_stack_sp), .data(valRam), .str(ram_store), .clk(clock),
    .ld(ram_load), .clr(reset));  // open: sel

  // Notes on the sheet:
  //   Axel SECHET
  //   Simon ROZEC
  //   Horloge et réinitialisation de la machine
  //   pile d'appels
  //   stackC
  //   choix de la valeur à stocker dans la pile
  //   stack
  //   Testeur
  //   PC updater
  //   mémoire ROM
  //   Controleur
  //   contents of rom_1 (hex, n*v repeats v):
  //   440b 4479 5405 5000 6000 5c00 4400 3000 3c11 5002 5001 4802 4801 4802 1400 5405 3812 4c00 5800
  //   mémoire RAM
  //   signaux
endmodule

module SP_register (
  input  [1:0] spsel,
  input  clock,
  input  reset,
  output [3:0] sp___1,
  output [3:0] sp,
  output [3:0] sp___1_2
);

  wire or_1_out, or_2_out, sp_nop, sp_pop, sp_push, sp_reset;

  Decoder #(.select(2), .enable("false")) decoder_1 (
    .out0(sp_reset), .out1(sp_pop), .out2(sp_nop), .out3(sp_push), .sel(spsel));
  or or_1 (or_1_out, sp_push, sp_pop);
  or or_2 (or_2_out, sp_reset, sp_push);
  Counter #(.width(4), .max('hf)) u_SP (
    .load(or_2_out), .D(4'b0000), .count(or_1_out), .Q(sp), .clk(clock), .clr(reset));  // open: carry
  Adder #(.width(4)) adder_1 (.a(4'b0001), .b(sp), .out(sp___1));  // open: cin, cout
  Subtractor #(.width(4)) subtractor_1 (.a(sp), .b(4'b0001), .out(sp___1_2));  // open: bin, bout

  // Notes on the sheet:
  //   Modification de SP en fonction de SPsel
endmodule

module Stack (
  input  [15:0] Input,
  input  [1:0] SPsel,
  input  Clock,
  input  [1:0] Wsel,
  input  reset,
  output [15:0] stack_sp,
  output [15:0] stack_sp_1
);

  wire nand_1_out, r0ac, r1ac, r2ac, r3ac, r4ac, r5ac, r6ac, r7ac, r8ac, r9ac, r10ac, r11ac, r12ac, r13ac,
       r14ac, r15ac;
  wire [3:0] multiplexer_1_out, sp, sp_1, sp_1_t;
  wire [15:0] r0, r1, r2, r3, r4, r5, r6, r7, r8, r9, r10, r11, r12, r13, r14, r15;

  Multiplexer #(.select(2), .width(4), .enable("false")) multiplexer_1 (
    .in0(sp), .in1(sp_1_t), .in2(sp_1), .out(multiplexer_1_out), .sel(Wsel));  // open: in3
  Decoder #(.select(4), .disabled(0)) decoder_1 (
    .out0(r0ac), .out1(r1ac), .out2(r2ac), .out3(r3ac), .out4(r4ac), .out5(r5ac), .out6(r6ac), .out7(r7ac),
    .out8(r8ac), .out9(r9ac), .out10(r10ac), .out11(r11ac), .out12(r12ac), .out13(r13ac), .out14(r14ac),
    .out15(r15ac), .sel(multiplexer_1_out), .en(nand_1_out));
  nand nand_1 (nand_1_out, Wsel[0], Wsel[1]);
  Register #(.width(16)) register_1 (.D(Input), .en(r0ac), .Q(r0), .clk(Clock), .clr(reset));
  Register #(.width(16)) register_2 (.D(Input), .en(r2ac), .Q(r2), .clk(Clock), .clr(reset));
  Register #(.width(16)) register_3 (.D(Input), .en(r1ac), .Q(r1), .clk(Clock), .clr(reset));
  Register #(.width(16)) register_4 (.D(Input), .en(r3ac), .Q(r3), .clk(Clock), .clr(reset));
  Register #(.width(16)) register_5 (.D(Input), .en(r4ac), .Q(r4), .clk(Clock), .clr(reset));
  SP_register sp_register_1 (.sp___1(sp_1), .sp(sp), .sp___1_2(sp_1_t), .spsel(SPsel), .clock(Clock), .reset(reset));
  Register #(.width(16)) register_6 (.D(Input), .en(r5ac), .Q(r5), .clk(Clock), .clr(reset));
  Register #(.width(16)) register_7 (.D(Input), .en(r6ac), .Q(r6), .clk(Clock), .clr(reset));
  Register #(.width(16)) register_8 (.D(Input), .en(r7ac), .Q(r7), .clk(Clock), .clr(reset));
  // Probe on sp_1
  // Probe on sp
  // Probe on sp_1_t
  Register #(.width(16)) register_9 (.D(Input), .en(r8ac), .Q(r8), .clk(Clock), .clr(reset));
  Register #(.width(16)) register_10 (.D(Input), .en(r10ac), .Q(r10), .clk(Clock), .clr(reset));
  Register #(.width(16)) register_11 (.D(Input), .en(r9ac), .Q(r9), .clk(Clock), .clr(reset));
  Register #(.width(16)) register_12 (.D(Input), .en(r11ac), .Q(r11), .clk(Clock), .clr(reset));
  Register #(.width(16)) register_13 (.D(Input), .en(r12ac), .Q(r12), .clk(Clock), .clr(reset));
  Register #(.width(16)) register_14 (.D(Input), .en(r14ac), .Q(r14), .clk(Clock), .clr(reset));
  Register #(.width(16)) register_15 (.D(Input), .en(r13ac), .Q(r13), .clk(Clock), .clr(reset));
  Multiplexer #(.select(4), .width(16), .enable("false")) multiplexer_2 (
    .in0(r0), .in1(r1), .in2(r2), .in3(r3), .in4(r4), .in5(r5), .in6(r6), .in7(r7), .in8(r8), .in9(r9),
    .in10(r10), .in11(r11), .in12(r12), .in13(r13), .in14(r14), .in15(r15), .out(stack_sp), .sel(sp));
  Register #(.width(16)) register_16 (.D(Input), .en(r15ac), .Q(r15), .clk(Clock), .clr(reset));
  Multiplexer #(.select(4), .width(16), .enable("false")) multiplexer_3 (
    .in0(r0), .in1(r1), .in2(r2), .in3(r3), .in4(r4), .in5(r5), .in6(r6), .in7(r7), .in8(r8), .in9(r9),
    .in10(r10), .in11(r11), .in12(r12), .in13(r13), .in14(r14), .in15(r15), .out(stack_sp_1), .sel(sp_1));

  // Notes on the sheet:
  //   Entrées
  //   définition des registres actif en fonction du pointeur de pile
  //   et du mode d'utilisation de la pile dans lequel on se trouve pour l'instruction actuelle
  //   r[n]ac = 1 si le registre [n] est actif, 0 sinon
  //   module de mise à jour et de lecture du pointeur de pile
  //   Sorties (valeur du registre [sp] et [sp+1])
  //   <- registres de la pile 
endmodule

module ALU (
  input  [15:0] A,
  input  [15:0] B,
  input  [3:0] op,
  output [15:0] C,
  output [2:0] flags,
  output CBout
);

  wire add_o, and_2_out, and_3_out, and_4_out, and_5_out, bitselector_3_out, bitselector_4_out,
       bitselector_5_out, bitselector_6_out, bitselector_7_out, bitselector_8_out, borrow, carry, or_4_out,
       sub_o;
  wire [3:0] bitselector_1_out, bitselector_2_out;
  wire [15:0] add, \and , div, mul, neg, \not , \or , rem, shl, sra, sub;

  BitSelector #(.width(16), .group(4)) bitselector_1 (.in(A), .out(bitselector_1_out), .sel(2'b00));
  BitSelector #(.width(16), .group(4)) bitselector_2 (.in(A), .out(bitselector_2_out), .sel(2'b00));
  Adder #(.width(16)) adder_1 (.a(A), .b(B), .out(add), .cout(carry));  // open: cin
  Subtractor #(.width(16)) subtractor_1 (.a(B), .b(A), .out(sub), .bout(borrow));  // open: bin
  Negator #(.width(16)) negator_1 (.in(B), .out(neg));
  Multiplier #(.width(16)) multiplier_1 (.a(A), .b(B), .out(mul));  // open: cin, cout
  Divider #(.width(16)) divider_1 (.a(B), .b(A), .out(div), .rem(rem));  // open: upper
  assign \not  = ~B;  // NOT_Gate not_1, 16 bits wide
  assign \and  = A & B;  // AND_Gate and_1, 16 bits wide
  assign \or  = A | B;  // OR_Gate or_1, 16 bits wide
  Shifter #(.width(16)) shifter_1 (.in(B), .\dist (bitselector_1_out), .out(shl));
  Shifter #(.width(16), .shift("lr")) shifter_2 (.in(B), .\dist (bitselector_2_out), .out(sra));
  BitSelector #(.width(16)) bitselector_3 (.in(A), .out(bitselector_3_out), .sel(4'b1111));
  BitSelector #(.width(16)) bitselector_4 (.in(B), .out(bitselector_4_out), .sel(4'b1111));
  BitSelector #(.width(16)) bitselector_5 (.in(add), .out(bitselector_5_out), .sel(4'b1111));
  BitSelector #(.width(16)) bitselector_6 (.in(B), .out(bitselector_6_out), .sel(4'b1111));
  BitSelector #(.width(16)) bitselector_7 (.in(A), .out(bitselector_7_out), .sel(4'b1111));
  BitSelector #(.width(16)) bitselector_8 (.in(sub), .out(bitselector_8_out), .sel(4'b1111));
  and and_2 (and_2_out, ~bitselector_3_out, ~bitselector_4_out, bitselector_5_out);  // AND_Gate
  and and_3 (and_3_out, bitselector_3_out, bitselector_4_out, ~bitselector_5_out);  // AND_Gate
  and and_4 (and_4_out, ~bitselector_6_out, bitselector_7_out, bitselector_8_out);  // AND_Gate
  and and_5 (and_5_out, bitselector_6_out, ~bitselector_7_out, ~bitselector_8_out);  // AND_Gate
  or or_2 (add_o, and_2_out, and_3_out);
  or or_3 (sub_o, and_4_out, and_5_out);
  or or_4 (or_4_out, op[3], op[2], op[1], op[0]);
  Multiplexer #(.enable("false")) multiplexer_1 (.in0(carry), .in1(borrow), .out(CBout), .sel(or_4_out));
  Multiplexer #(.select(4), .width(16), .enable("false")) multiplexer_2 (
    .in0(add), .in1(sub), .in2(neg), .in3(mul), .in4(div), .in5(rem), .in6(\not ), .in7(\and ), .in8(\or ),
    .in9(shl), .in10(sra), .in11(sub), .in12(sub), .in13(sub), .out(C), .sel(op));  // open: in14, in15
  nor nor_1 (flags[0], C[15], C[14], C[13], C[12], C[11], C[10], C[9], C[8], C[7], C[6], C[5], C[4], C[3], C[2], C[1], C[0]);
  Multiplexer #(.enable("false")) multiplexer_3 (.in0(add_o), .in1(sub_o), .out(flags[2]), .sel(or_4_out));

  assign flags[1] = C[15];

  // Other names for the same wires on the sheet: zf = flags[0]; sf = C[15]; of = flags[2]

  // Notes on the sheet:
  //   Entrées
  //   Calculs sur les entrées
  //   calculs de l'overflow dans le cas d'une addition 
  //   ou d'une soustraction
  //   définition de CBout en fonction de l'opération
  //   choix de la bonne valeur de sortie en fonction de l'instruction actuelle
  //   définition de l'overflow de sortie
endmodule

module Tester (
  input  [5:0] op,
  input  [2:0] flags,
  output [15:0] \output 
);

  wire gt, lt, multiplexer_1_out, or_1_out;
  wire [4:0] bitselector_1_out;

  and and_1 (lt, ~flags[0], flags[1], ~flags[2]);  // AND_Gate
  and and_2 (gt, ~flags[0], or_1_out);  // AND_Gate
  or or_1 (or_1_out, ~flags[1], flags[2]);  // OR_Gate
  BitSelector #(.width(6), .group(5)) bitselector_1 (.in(op), .out(bitselector_1_out), .sel(1'b0));
  assign \output  = {{15{1'b0}}, multiplexer_1_out};  // Bit_Extender bit_extender_1
  Multiplexer #(.select(5), .enable("false")) multiplexer_1 (
    .in11(lt), .in12(flags[0]), .in13(gt), .out(multiplexer_1_out), .sel(bitselector_1_out));  // open: in0, in1, in2, in3, in4, in5, in6, in7, in8, in9, in10, in14, in15, in16, in17, in18, in19, in20, in21, in22, in23, in24, in25, in26, in27, in28, in29, in30, in31

  // Other names for the same wires on the sheet: eq = flags[0]; zf = flags[0]; sf = flags[1]; of = flags[2]

  // Notes on the sheet:
  //   Entrées
  //   calcul des valeurs des tests en fonction des flags en sortie de l'ALU
  //   choix de la valeur de test en fonction de l'opération actuelle
endmodule

module PC_updater (
  input  [5:0] op,
  input  [9:0] adrInstr,
  input  [15:0] pc,
  input  [15:0] call_stack,
  input  [15:0] stack_top,
  output [15:0] next_pc,
  output [15:0] pc___1
);

  wire bitselector_1_out, bitselector_2_out;
  wire [4:0] bitselector_3_out;
  wire [15:0] adrinst, jumpcondf, jumpcondt;

  assign adrinst = {{6{1'b0}}, adrInstr};  // Bit_Extender bit_extender_1
  Adder #(.width(16)) adder_1 (.a(pc), .b(16'h1), .out(pc___1));  // open: cin, cout
  BitSelector #(.width(16)) bitselector_1 (.in(stack_top), .out(bitselector_1_out), .sel(4'b0000));
  Multiplexer #(.width(16), .enable("false")) multiplexer_1 (
    .in0(pc___1), .in1(adrinst), .out(jumpcondt), .sel(bitselector_1_out));
  BitSelector #(.width(16)) bitselector_2 (.in(stack_top), .out(bitselector_2_out), .sel(4'b0000));
  Multiplexer #(.width(16), .enable("false")) multiplexer_2 (
    .in0(adrinst), .in1(pc___1), .out(jumpcondf), .sel(bitselector_2_out));
  BitSelector #(.width(6), .group(5)) bitselector_3 (.in(op), .out(bitselector_3_out), .sel(1'b0));
  Multiplexer #(.select(5), .width(16), .enable("false")) multiplexer_3 (
    .in0(pc___1), .in1(pc___1), .in2(pc___1), .in3(pc___1), .in4(pc___1), .in5(pc___1), .in6(pc___1),
    .in7(pc___1), .in8(pc___1), .in9(pc___1), .in10(pc___1), .in11(pc___1), .in12(pc___1), .in13(pc___1),
    .in14(adrinst), .in15(jumpcondt), .in16(jumpcondf), .in17(pc___1), .in18(pc___1), .in19(pc___1),
    .in20(pc___1), .in21(adrinst), .in22(call_stack), .in23(pc___1), .in24(pc___1), .out(next_pc),
    .sel(bitselector_3_out));  // open: in25, in26, in27, in28, in29, in30, in31

  // Other names for the same wires on the sheet: callstack[15:0] = call_stack; pc_1[15:0] = pc___1;
  //   stacktop[15:0] = stack_top

  // Notes on the sheet:
  //   Entrées
  //   calcul des nouvelles adresses potentielles
  //   Choix de la prochaine adresse en fonction de l'instruction à éxécuter
  //   pc+1 est envoyé en sortie pour pouvoir être empilé sur la callstack lors d'une instruction call
endmodule

module Controller (
  input  [5:0] op,
  output [1:0] stackc_wsel,
  output [1:0] stackc_spsel,
  output [1:0] stack_wsel,
  output [1:0] stack_spsel,
  output [2:0] stack_mux,
  output sig_halt,
  output ram_load,
  output ram_store
);

  wire [7:6] rom_2_data;

  ROM #(.addrWidth(6)) rom_1 (.addr(op), .data({stack_spsel, stack_wsel, stackc_spsel, stackc_wsel}));  // open: sel
  ROM #(.addrWidth(6)) rom_2 (.addr(op), .data({rom_2_data, ram_store, ram_load, sig_halt, stack_mux}));  // open: sel

  // Notes on the sheet:
  //   valeurs d'entrée des deux piles
  //   signal du multiplexeur
  //   définition des signaux en fonction de l'instruction à éxécuter
  //   contents of rom_1 (hex, n*v repeats v):
  //   6b 6b 8b 6b 6b 6b 8b 7*6b bb 7b 7b db db 7b 7b bd b7 db bb
  //   contents of rom_2 (hex, n*v repeats v):
  //   11*3 4 4 4 0 0 0 2 11 0 20 0 0 0 8
endmodule
